# Fritzing sketch OpenSensor (saved by Fritzing 1.0.4)

parts:
  A1 = ESP32-S3-WROOM-1-N16R8 dev board
  M1 = ph-4502c [package=THT]
  Part1 = ADS1115
  OLED_I2C1 = OLED 128x64 I2C Monochrome Display
  A2 = tds-sensor-meter-v1.0_1

nets:
  N1: A1.Pin_1, A1.Pin_2, A2.pin2
  N2: A1.Pin_12, Part1.SDA, OLED_I2C1.SDA
  N3: A1.Pin_15, Part1.SCL, OLED_I2C1.SCK
  VDD: A1.Pin_21, M1.pin6, Part1.VDD, OLED_I2C1.VDD
  GND: A1.Pin_22, M1.pin4, M1.pin5, Part1.GND, OLED_I2C1.GND, A2.pin3
  N4: M1.pin3, Part1.A0

notes:
  SDA
  SCL

custom parts:
  ESP32-S3-WROOM-1-N16R8 dev board: ESP32-S3 WIFI+BLE5.0 Development Board ESP32-S3-WROOM-1-N16R8(16M Flash/8SRAM).
  ph-4502c: ph-4502c PH Meter.
  ADS1115: ADC ADS1115
  : TDS Meter V1.0 Development Board Water Meter Filter Measuring Water Sensor Module.

// code stored in the sketch: old.ino
#static const uint8_t SDA = 8;
#static const uint8_t SCL = 9;
